# Fritzing sketch smartLock_squematic (saved by Fritzing 0.9.3b)

parts:
  U2 = atmega328 [package=dip]
  U3 = Voltage Regulator - 3.3V [package="TO220 [THT]"]
  U4 = Voltage Regulator - 5V [package="TO220 [THT]"]
  R1 = Resistor [tolerance=±5% resistance=10k package="2010 [SMD]"]
  XTAL1 = Crystal [frequency="16 Mhz" package=THT]
  C1 = Capacitor [package=cap-pth-small2]
  C2 = Capacitor [package=cap-pth-small2]
  Componente1 = RFID-RC522-v2
  U5 = ESP8266 WiFi Module [part_number=ESP8266]
  J1 = Basic Servo
  S1 = Pushbutton [package=THT]
  R2 = Resistor [tolerance=±5% resistance=2k package="2010 [SMD]"]
  R3 = Resistor [tolerance=±5% resistance=3k package="2010 [SMD]"]
  J2 = Piezo Speaker

nets:
  N1: U2.RESET, R1.Pin_1
  N2: U2.D2, R2.Pin_1
  N3: U2.D3_(PWM), U5.TXD
  N4: U2.D4, J1.pulse
  VCC: U2.VCC, U4.output_voltage, R1.Pin_0, J1.vcc
  GND: U2.GND, U3.GND, U4.GND, C1.1, C2.2, Componente1.GND, U5.GND, J1.gnd, S1.leg1, R3.Pin_0, J2.pin2
  N5: U2.XLAT1, XTAL1.pin_1, C1.2
  N6: U2.XLAT2, C2.1
  N7: U2.D5_(PWM), S1.leg0
  N8: U2.D6_(PWM), J2.pin1
  N9: U2.D9_(PWM), Componente1.RST
  N10: U2.D10_(PWM), Componente1.SDA
  N11: U2.D11_(PWM), Componente1.MOSI
  N12: U2.D12, Componente1.MISO
  N13: U2.D13, Componente1.SCK
  N14: U3.input_voltage, U4.input_voltage
  3.3V: U3.output_voltage, Componente1.3.3V, U5.VCC, U5.RST, U5.CH_PD
  N15: U5.RXD, R2.Pin_0, R3.Pin_1

custom parts:
  RFID-RC522-v2: A simple China made RFID-RC522 Reader; do check the pin labels, as this is a MFRC522 based clone.
  ESP8266 WiFi Module: Generic WiFi Module based on the ESP8266 with onboard PCB antenna and UART communications
